# Fritzing sketch green_twinkler_0_8_7 (saved by Fritzing 0.8.7b)
circuit board: 6.1cm x 4.6cm
breadboards: 1

parts:
  V1 = DC Power [voltage=3.3V]
  S1 = Toggle Switch [package=THT]
  IC1 = ATtiny814 SOIC [chip_label="ATtiny814 SOIC" package=SOIC-14]
  XTAL1 = CRYSTAL - kHz [frequency="32 kHz"]
  C2 = Ceramic Capacitor [capacitance=12pF package="100 mil [THT, multilayer]"]
  C3 = Ceramic Capacitor [capacitance=12pF package="100 mil [THT, multilayer]"]
  R3 = Resistor [tolerance=±5% resistance=130 package=THT]
  R4 = Resistor [tolerance=±5% resistance=130 package=THT]
  R5 = Resistor [tolerance=±5% resistance=4.7k package=THT]
  R6 = Resistor [tolerance=±10% resistance=4.7k package=THT]
  R7 = Resistor [tolerance=±5% resistance=4.7k package=THT]
  Q1 = PNP-Transistor [package="SOT-23 [SMD]"]
  Q2 = PNP-Transistor [package="SOT-23 [SMD]"]
  Q3 = PNP-Transistor [package="SOT-23 [SMD]"]
  LED2 = smd LED [color="Green (570nm)" package="0805 [SMD]"]
  LED1 = smd LED [color="Green (570nm)" package="0805 [SMD]"]
  LED3 = smd LED [color="Green (570nm)" package="0805 [SMD]"]
  J1 = AVR UPDI [package=2x3_lock]
  C1 = Ceramic Capacitor [capacitance="100 nF" package="0805 [SMD, multilayer]"]
  R2 = Resistor [tolerance=±5% resistance=130 package=THT]

nets:
  N1: V1.V+, S1.COM
  N2: V1.V-, IC1.14, C2.0, C3.0, Q1.2, Q2.2, Q3.2, J1.6, C1.1
  N3: S1.L1, IC1.1, R3.Pin_1, R4.Pin_1, J1.2, C1.0, R2.Pin_1
  N4: IC1.2, R6.Pin_0
  N5: IC1.3, R7.Pin_0
  N6: IC1.6, XTAL1.pin_0, C2.1
  N7: IC1.7, XTAL1.pin_1, C3.1
  N8: IC1.10, J1.1
  N9: IC1.13, R5.Pin_0
  N10: R3.Pin_0, LED2.anode
  N11: R4.Pin_0, LED3.anode
  N12: R5.Pin_1, Q1.0
  N13: R6.Pin_1, Q2.0
  N14: R7.Pin_1, Q3.0
  N15: Q1.1, LED1.cathode
  N16: Q2.1, LED2.cathode
  N17: Q3.1, LED3.cathode
  N18: LED1.anode, R2.Pin_0

notes:
  VCC

custom parts:
  AVR UPDI: AVR UPDI Plug (Male)
